// Logisim project SnakeGame.circ as structural Verilog: 24 circuits, main circuit main
module main (
);

  wire A_out, and_1_out, and_3_out, and_4_out, and_5_out, and_6_out, and_7_out, clock_1_out, comparator_1_lt,
       comparator_2_eq, comparator_3_eq, comparator_4_eq, comparator_5_eq, comparator_6_eq, comparator_7_eq,
       Coordenadas_da_maca, counter_5_carry, counter_8_q, D_out, demultiplexer_3_out0, demultiplexer_3_out1,
       demultiplexer_3_out2, demultiplexer_4_out0, demultiplexer_4_out2, demultiplexer_5_out0,
       demultiplexer_5_out1, Desenha_maca, Display_clock, Incrementa_tamanho_da_cobrinha,
       Incremento_da_cabeca, Inicializacao_de_direcao, Inicializador_da_cabeca_da_cobra,
       Inicializador_da_maca, Inicializador_de_tamanho, Input_controller_parte_de_reset, Loop_principal, M1,
       M1_Clock, M2, M2_Clock, M3, M3_Clock, M4, M4__2, M4_Clock, Maca_encontrada, Memory_clock_M4,
       multiplexer_5_out, not_1_out, not_2_out, not_3_out, Operation_counter_q, or_1_out, or_2_out, or_3_out,
       or_4_out, or_5_out, or_6_out, Perdeu, S_out, Venceu, W_out;
  wire [1:0] counter_4_q, Module_num;
  wire [1:1] counter_6_q;
  wire [2:0] counter_1_q;
  wire [3:0] exibicao_do_digito_da_coordenada_da_maca_1_out_3,
       exibicao_do_digito_da_coordenada_da_maca_1_out_4, exibicao_do_digito_da_coordenada_da_maca_1_out_5,
       exibicao_do_digito_da_coordenada_da_maca_1_out_6;
  wire [4:0] controlled_buffer_3_out, controlled_buffer_4_out, Direcao_X, Direcao_Y, Maca_X, Maca_Y,
       modulo_de_movimentacao_da_cobra_1_nova_coordenada_de_x,
       modulo_de_movimentacao_da_cobra_1_nova_coordenada_em_y, multiplexer_3_out, multiplexer_4_out,
       register_1_q, register_2_q, register_3_q, register_4_q, register_5_q, register_6_q, X, X__M4, Y, Y__M4;
  wire [6:0] keyboard_1_data;
  wire [7:0] adder_1_out, Address_for_shifter, counter_3_q, M3_Address, M4_Address, multiplexer_1_out,
       multiplexer_2_out, Posicao_da_cabeca_da_cobrinha, Tamanho_da_cobrinha;
  wire [31:0] circuito_de_exibicao_em_tela_32_bits_1_out_7, circuito_de_exibicao_em_tela_32_bits_1_out_8,
       circuito_de_exibicao_em_tela_32_bits_1_out_9, circuito_de_exibicao_em_tela_32_bits_1_out_10,
       circuito_de_exibicao_em_tela_32_bits_1_out_11, circuito_de_exibicao_em_tela_32_bits_1_out_12,
       circuito_de_exibicao_em_tela_32_bits_1_out_13, circuito_de_exibicao_em_tela_32_bits_1_out_14,
       circuito_de_exibicao_em_tela_32_bits_1_out_15, circuito_de_exibicao_em_tela_32_bits_1_out_16,
       circuito_de_exibicao_em_tela_32_bits_1_out_17, circuito_de_exibicao_em_tela_32_bits_1_out_18,
       circuito_de_exibicao_em_tela_32_bits_1_out_19, circuito_de_exibicao_em_tela_32_bits_1_out_20,
       circuito_de_exibicao_em_tela_32_bits_1_out_21, circuito_de_exibicao_em_tela_32_bits_1_out_22,
       circuito_de_exibicao_em_tela_32_bits_1_out_23, circuito_de_exibicao_em_tela_32_bits_1_out_24,
       circuito_de_exibicao_em_tela_32_bits_1_out_25, circuito_de_exibicao_em_tela_32_bits_1_out_26,
       circuito_de_exibicao_em_tela_32_bits_1_out_27, circuito_de_exibicao_em_tela_32_bits_1_out_28,
       circuito_de_exibicao_em_tela_32_bits_1_out_29, circuito_de_exibicao_em_tela_32_bits_1_out_30,
       circuito_de_exibicao_em_tela_32_bits_1_out_31, circuito_de_exibicao_em_tela_32_bits_1_out_32,
       circuito_de_exibicao_em_tela_32_bits_1_out_33, circuito_de_exibicao_em_tela_32_bits_1_out_34,
       circuito_de_exibicao_em_tela_32_bits_1_out_35, circuito_de_exibicao_em_tela_32_bits_1_out_36,
       circuito_de_exibicao_em_tela_32_bits_1_out_37, circuito_de_exibicao_em_tela_32_bits_1_out_38;

  Demultiplexer #(.select(3)) demultiplexer_1 (
    .out0(Inicializador_de_tamanho), .out1(Inicializador_da_cabeca_da_cobra),
    .out2(Inicializacao_de_direcao), .out3(Inicializador_da_maca), .out4(Loop_principal), .in(clock_1_out),
    .sel(counter_1_q));  // open: out5, out6, out7, en
  Clock clock_1 (.out(clock_1_out));
  Counter #(.width(3), .max('h7), .trigger("falling")) counter_1 (
    .Q(counter_1_q), .clk(or_2_out), .clr(or_1_out));  // open: load, D, count, carry
  or or_1 (or_1_out, Perdeu, Venceu);
  or or_2 (or_2_out, Inicializador_de_tamanho, Inicializador_da_cabeca_da_cobra, Inicializacao_de_direcao, counter_5_carry);
  Demultiplexer #(.select(2)) demultiplexer_2 (
    .out0(M1_Clock), .out1(M2_Clock), .out2(M3_Clock), .out3(M4_Clock), .in(Loop_principal), .sel(Module_num));  // open: en
  Counter #(.width(2), .max('h3), .trigger("falling")) counter_2 (
    .Q(Module_num), .clk(or_3_out));  // open: load, D, count, carry, clr
  or or_3 (or_3_out, M1, M2, M3, M4);
  Hex_Digit_Display hex_digit_display_1 (.value(Tamanho_da_cobrinha[7:4]));  // open: dp
  Hex_Digit_Display hex_digit_display_2 (.value(Tamanho_da_cobrinha[3:0]));  // open: dp
  Modulo_de_movimentacao_da_cobra modulo_de_movimentacao_da_cobra_1 (
    .Clock__entrada(M1_Clock), .\Coordenada_da_cabeça_em_Y (Y), .\Coordenada_da_cabeça_em_X (X),
    .\Direção_em_X (Direcao_X), .\Direção_em_Y (Direcao_Y), .out_9(M2),
    .Nova_coordenada_em_Y(modulo_de_movimentacao_da_cobra_1_nova_coordenada_em_y),
    .Nova_coordenada_de_X(modulo_de_movimentacao_da_cobra_1_nova_coordenada_de_x),
    .\Incremento_da_cabeça_da_cobrinha___Conta_a_posição_da_mesma (Incremento_da_cabeca));
  Modulo_de_exibicao_em_tela modulo_de_exibicao_em_tela_1 (
    .Tamnho_da_cobrinha__entrada(Tamanho_da_cobrinha), .Clock__entrada(M2_Clock),
    .\Ponto_de_finalização_do_pulso_do_clock (M1), .\Clock__saída (Display_clock));  // open: Localização_da_saída
  assign M3_Address = demultiplexer_5_out0 ? Posicao_da_cabeca_da_cobrinha : 8'bz;  // Controlled_Buffer controlled_buffer_1
  Counter #(.trigger("falling")) counter_3 (
    .Q(counter_3_q), .clk(demultiplexer_5_out1), .clr(comparator_2_eq));  // open: load, D, count, carry
  assign M3_Address = not_1_out ? counter_3_q : 8'bz;  // Controlled_Buffer controlled_buffer_2
  not not_1 (not_1_out, demultiplexer_5_out0);
  Demultiplexer #(.select(2)) demultiplexer_3 (
    .out0(demultiplexer_3_out0), .out1(demultiplexer_3_out1), .out2(demultiplexer_3_out2), .in(M4_Clock),
    .sel(counter_4_q));  // open: out3, en
  Counter #(.width(2), .max('h2)) counter_4 (
    .Q(counter_4_q), .clk(or_4_out), .clr(demultiplexer_4_out2));  // open: load, D, count, carry
  or or_4 (or_4_out, Maca_encontrada, M4__2);
  Comparator #(.mode("unsigned")) comparator_1 (
    .a({8{1'b0}}), .b(Tamanho_da_cobrinha), .lt(comparator_1_lt));  // open: gt, eq
  Comparator #(.mode("unsigned")) comparator_2 (
    .a(Tamanho_da_cobrinha), .b(M3_Address), .eq(comparator_2_eq));  // open: gt, lt
  and and_1 (and_1_out, not_2_out, counter_4_q[0]);
  not not_2 (not_2_out, counter_4_q[1]);
  or or_5 (or_5_out, demultiplexer_3_out2, Inicializador_da_maca);
  Hex_Digit_Display hex_digit_display_3 (.value(exibicao_do_digito_da_coordenada_da_maca_1_out_3));  // open: dp
  Counter #(.width(3), .max('h3), .trigger("falling")) counter_5 (
    .carry(counter_5_carry), .clk(Inicializador_da_maca), .clr(counter_5_carry));  // open: load, D, count, Q
  Multiplexer #(.select(2), .width(8)) multiplexer_1 (
    .in0(Posicao_da_cabeca_da_cobrinha), .in1(Posicao_da_cabeca_da_cobrinha), .in2(M3_Address),
    .in3(M4_Address), .out(multiplexer_1_out), .sel(Module_num));  // open: en
  Multiplexer #(.select(2), .width(8)) multiplexer_2 (
    .in0(Posicao_da_cabeca_da_cobrinha), .in1(Posicao_da_cabeca_da_cobrinha), .in2(M3_Address),
    .in3(M4_Address), .out(multiplexer_2_out), .sel(Module_num));  // open: en
  Multiplexer #(.select(2), .width(5)) multiplexer_3 (
    .in0(modulo_de_movimentacao_da_cobra_1_nova_coordenada_em_y), .in3(Y__M4), .out(multiplexer_3_out),
    .sel(Module_num));  // open: in1, in2, en
  Multiplexer #(.select(2), .width(5)) multiplexer_4 (
    .in0(modulo_de_movimentacao_da_cobra_1_nova_coordenada_de_x), .in3(X__M4), .out(multiplexer_4_out),
    .sel(Module_num));  // open: in1, in2, en
  Multiplexer #(.select(2)) multiplexer_5 (
    .in0(M2), .in1(1'b0), .in2(1'b0), .in3(Memory_clock_M4), .out(multiplexer_5_out), .sel(Module_num));  // open: en
  and and_2 (M3, comparator_1_lt, comparator_2_eq);
  Multiplexer #(.width(8)) multiplexer_6 (
    .in0(Posicao_da_cabeca_da_cobrinha), .in1(Address_for_shifter), .out(M4_Address), .sel(and_1_out));  // open: en
  Demultiplexer #(.select(2)) demultiplexer_4 (
    .out0(demultiplexer_4_out0), .out1(Desenha_maca), .out2(demultiplexer_4_out2), .in(or_5_out),
    .sel({counter_6_q[1], Coordenadas_da_maca}));  // open: out3, en
  Counter #(.width(2), .max('h2), .trigger("falling")) counter_6 (
    .Q({counter_6_q[1], Coordenadas_da_maca}), .clk(or_5_out));  // open: load, D, count, carry, clr
  Hex_Digit_Display hex_digit_display_4 (.value(exibicao_do_digito_da_coordenada_da_maca_1_out_5));  // open: dp
  Hex_Digit_Display hex_digit_display_5 (.value(exibicao_do_digito_da_coordenada_da_maca_1_out_4));  // open: dp
  Exibicao_do_digito_da_coordenada_da_maca exibicao_do_digito_da_coordenada_da_maca_1 (
    .in_1(Maca_X), .in_2(Maca_Y), .out_3(exibicao_do_digito_da_coordenada_da_maca_1_out_3),
    .out_4(exibicao_do_digito_da_coordenada_da_maca_1_out_4),
    .out_5(exibicao_do_digito_da_coordenada_da_maca_1_out_5),
    .out_6(exibicao_do_digito_da_coordenada_da_maca_1_out_6));
  Register #(.width(5), .trigger("high")) register_1 (
    .D(X), .Q(register_1_q), .clk(demultiplexer_3_out0));  // open: en, clr
  Register #(.width(5), .trigger("high")) register_2 (
    .D(Y), .Q(register_2_q), .clk(demultiplexer_3_out0));  // open: en, clr
  Random #(.width(5)) random_1 (.clk(demultiplexer_4_out0), .out(Maca_X));  // open: next, clr
  Random #(.width(5), .seed(1)) random_2 (.clk(demultiplexer_4_out0), .out(Maca_Y));  // open: next, clr
  Adder adder_1 (.a(Posicao_da_cabeca_da_cobrinha), .b(8'h1), .out(adder_1_out));  // open: cin, cout
  Hex_Digit_Display hex_digit_display_6 (.value(exibicao_do_digito_da_coordenada_da_maca_1_out_6));  // open: dp
  RAM #(.dataWidth(5), .bus("separate")) ram_1 (
    .addr(multiplexer_1_out), .din(multiplexer_3_out), .data(Y), .clk(multiplexer_5_out));  // open: str, sel, ld, clr
  RAM #(.dataWidth(5), .bus("separate")) ram_2 (
    .addr(multiplexer_2_out), .din(multiplexer_4_out), .data(X), .clk(multiplexer_5_out));  // open: str, sel, ld, clr
  Demultiplexer demultiplexer_5 (
    .out0(demultiplexer_5_out0), .out1(demultiplexer_5_out1), .in(M3_Clock), .sel(Operation_counter_q));  // open: en
  Counter #(.width(1), .max('h1), .trigger("falling")) Operation_counter (
    .Q(Operation_counter_q), .clk(demultiplexer_5_out0), .clr(comparator_2_eq));  // open: load, D, count, carry
  Comparator #(.mode("unsigned")) comparator_3 (
    .a(Posicao_da_cabeca_da_cobrinha), .b(M3_Address), .eq(comparator_3_eq));  // open: gt, lt
  Keyboard keyboard_1 (.clr(Input_controller_parte_de_reset), .data(keyboard_1_data));  // open: clk, re, avail
  Button A (.out(A_out));
  not not_3 (not_3_out, Coordenadas_da_maca);
  assign controlled_buffer_3_out = not_3_out ? Y : 5'bz;  // Controlled_Buffer controlled_buffer_3
  assign controlled_buffer_4_out = not_3_out ? X : 5'bz;  // Controlled_Buffer controlled_buffer_4
  Comparator #(.width(5), .mode("unsigned")) comparator_4 (
    .a(register_1_q), .b(Maca_X), .eq(comparator_4_eq));  // open: gt, lt
  Comparator #(.width(5), .mode("unsigned")) comparator_5 (
    .a(Maca_Y), .b(register_2_q), .eq(comparator_5_eq));  // open: gt, lt
  Modulo_de_crescimento_da_cobra modulo_de_crescimento_da_cobra_1 (
    .Tamanho_da_cobrinha(Tamanho_da_cobrinha), .\Posição_de_inicio (adder_1_out), .X(X), .Y(Y),
    .Clock(demultiplexer_3_out1), .\Ponto_de_saída_do_clock (Memory_clock_M4), .Marco_final(M4__2),
    .\Endereço_de_saída (Address_for_shifter), .\Saída_de_X (X__M4), .\Saída_de_Y (Y__M4));
  Button W (.out(W_out));
  Button S (.out(S_out));
  Button D (.out(D_out));
  assign controlled_buffer_3_out = Coordenadas_da_maca ? Maca_Y : 5'bz;  // Controlled_Buffer controlled_buffer_5
  assign controlled_buffer_4_out = Coordenadas_da_maca ? Maca_X : 5'bz;  // Controlled_Buffer controlled_buffer_6
  Register #(.width(5), .trigger("high")) register_3 (
    .D(controlled_buffer_4_out), .Q(register_3_q), .clk(Incremento_da_cabeca));  // open: en, clr
  Register #(.width(5), .trigger("high")) register_4 (
    .D(controlled_buffer_3_out), .Q(register_4_q), .clk(Incremento_da_cabeca));  // open: en, clr
  Register #(.width(5), .trigger("high")) register_5 (
    .D(X), .Q(register_5_q), .clk(demultiplexer_5_out0));  // open: en, clr
  Register #(.width(5), .trigger("high")) register_6 (
    .D(Y), .Q(register_6_q), .clk(demultiplexer_5_out0));  // open: en, clr
  and and_3 (and_3_out, comparator_4_eq, comparator_5_eq);
  and and_4 (and_4_out, demultiplexer_3_out0, and_3_out);
  Modulo_de_controle_do_teclado Input_controller (
    .D(D_out), .A(A_out), .S(S_out), .W(W_out), .Teclado(keyboard_1_data),
    .Parte_de_Reset(Input_controller_parte_de_reset), .in_3(Inicializacao_de_direcao),
    .\Direção_Eixo_X (Direcao_X), .\Direção_Eixo_Y (Direcao_Y));
  Counter #(.width(1), .max('h1)) counter_7 (
    .D(and_3_out), .Q(Incrementa_tamanho_da_cobrinha), .clk(and_3_out), .clr(Incrementa_tamanho_da_cobrinha));  // open: load, count, carry
  Counter #(.width(1), .max('h1), .trigger("falling")) counter_8 (
    .Q(counter_8_q), .clk(demultiplexer_3_out0));  // open: load, D, count, carry, clr
  Counter #(.width(1), .max('h1), .trigger("falling")) counter_9 (
    .Q(Maca_encontrada), .clk(and_4_out), .clr(Maca_encontrada));  // open: load, D, count, carry
  Circuito_de_exibicao_em_tela__32_bits circuito_de_exibicao_em_tela_32_bits_1 (
    .Clock(or_6_out), .\Posições_em_Y (controlled_buffer_3_out), .\Posições_em_X (controlled_buffer_4_out),
    .Reseta_a_coluna_numerada_em_uso(register_3_q), .Reseta_a_linha_numerada_em_uso(register_4_q),
    .Reseta_os_eixos__x__e__y(M2), .out_7(circuito_de_exibicao_em_tela_32_bits_1_out_7),
    .out_8(circuito_de_exibicao_em_tela_32_bits_1_out_8),
    .out_9(circuito_de_exibicao_em_tela_32_bits_1_out_9),
    .out_10(circuito_de_exibicao_em_tela_32_bits_1_out_10),
    .out_11(circuito_de_exibicao_em_tela_32_bits_1_out_11),
    .out_12(circuito_de_exibicao_em_tela_32_bits_1_out_12),
    .out_13(circuito_de_exibicao_em_tela_32_bits_1_out_13),
    .out_14(circuito_de_exibicao_em_tela_32_bits_1_out_14),
    .out_15(circuito_de_exibicao_em_tela_32_bits_1_out_15),
    .out_16(circuito_de_exibicao_em_tela_32_bits_1_out_16),
    .out_17(circuito_de_exibicao_em_tela_32_bits_1_out_17),
    .out_18(circuito_de_exibicao_em_tela_32_bits_1_out_18),
    .out_19(circuito_de_exibicao_em_tela_32_bits_1_out_19),
    .out_20(circuito_de_exibicao_em_tela_32_bits_1_out_20),
    .out_21(circuito_de_exibicao_em_tela_32_bits_1_out_21),
    .out_22(circuito_de_exibicao_em_tela_32_bits_1_out_22),
    .out_23(circuito_de_exibicao_em_tela_32_bits_1_out_23),
    .out_24(circuito_de_exibicao_em_tela_32_bits_1_out_24),
    .out_25(circuito_de_exibicao_em_tela_32_bits_1_out_25),
    .out_26(circuito_de_exibicao_em_tela_32_bits_1_out_26),
    .out_27(circuito_de_exibicao_em_tela_32_bits_1_out_27),
    .out_28(circuito_de_exibicao_em_tela_32_bits_1_out_28),
    .out_29(circuito_de_exibicao_em_tela_32_bits_1_out_29),
    .out_30(circuito_de_exibicao_em_tela_32_bits_1_out_30),
    .out_31(circuito_de_exibicao_em_tela_32_bits_1_out_31),
    .out_32(circuito_de_exibicao_em_tela_32_bits_1_out_32),
    .out_33(circuito_de_exibicao_em_tela_32_bits_1_out_33),
    .out_34(circuito_de_exibicao_em_tela_32_bits_1_out_34),
    .out_35(circuito_de_exibicao_em_tela_32_bits_1_out_35),
    .out_36(circuito_de_exibicao_em_tela_32_bits_1_out_36),
    .out_37(circuito_de_exibicao_em_tela_32_bits_1_out_37),
    .out_38(circuito_de_exibicao_em_tela_32_bits_1_out_38));
  DotMatrix #(.matrixcols(32), .matrixrows(32)) dotmatrix_1 (
    .col0(circuito_de_exibicao_em_tela_32_bits_1_out_7), .col1(circuito_de_exibicao_em_tela_32_bits_1_out_8),
    .col2(circuito_de_exibicao_em_tela_32_bits_1_out_9),
    .col3(circuito_de_exibicao_em_tela_32_bits_1_out_10),
    .col4(circuito_de_exibicao_em_tela_32_bits_1_out_11),
    .col5(circuito_de_exibicao_em_tela_32_bits_1_out_12),
    .col6(circuito_de_exibicao_em_tela_32_bits_1_out_13),
    .col7(circuito_de_exibicao_em_tela_32_bits_1_out_14),
    .col8(circuito_de_exibicao_em_tela_32_bits_1_out_15),
    .col9(circuito_de_exibicao_em_tela_32_bits_1_out_16),
    .col10(circuito_de_exibicao_em_tela_32_bits_1_out_17),
    .col11(circuito_de_exibicao_em_tela_32_bits_1_out_18),
    .col12(circuito_de_exibicao_em_tela_32_bits_1_out_19),
    .col13(circuito_de_exibicao_em_tela_32_bits_1_out_20),
    .col14(circuito_de_exibicao_em_tela_32_bits_1_out_21),
    .col15(circuito_de_exibicao_em_tela_32_bits_1_out_22),
    .col16(circuito_de_exibicao_em_tela_32_bits_1_out_23),
    .col17(circuito_de_exibicao_em_tela_32_bits_1_out_24),
    .col18(circuito_de_exibicao_em_tela_32_bits_1_out_25),
    .col19(circuito_de_exibicao_em_tela_32_bits_1_out_26),
    .col20(circuito_de_exibicao_em_tela_32_bits_1_out_27),
    .col21(circuito_de_exibicao_em_tela_32_bits_1_out_28),
    .col22(circuito_de_exibicao_em_tela_32_bits_1_out_29),
    .col23(circuito_de_exibicao_em_tela_32_bits_1_out_30),
    .col24(circuito_de_exibicao_em_tela_32_bits_1_out_31),
    .col25(circuito_de_exibicao_em_tela_32_bits_1_out_32),
    .col26(circuito_de_exibicao_em_tela_32_bits_1_out_33),
    .col27(circuito_de_exibicao_em_tela_32_bits_1_out_34),
    .col28(circuito_de_exibicao_em_tela_32_bits_1_out_35),
    .col29(circuito_de_exibicao_em_tela_32_bits_1_out_36),
    .col30(circuito_de_exibicao_em_tela_32_bits_1_out_37),
    .col31(circuito_de_exibicao_em_tela_32_bits_1_out_38));
  Comparator #(.width(5), .mode("unsigned")) comparator_6 (
    .a(register_5_q), .b(X), .eq(comparator_6_eq));  // open: gt, lt
  Comparator #(.width(5), .mode("unsigned")) comparator_7 (
    .a(Y), .b(register_6_q), .eq(comparator_7_eq));  // open: gt, lt
  and and_5 (and_5_out, counter_8_q, demultiplexer_3_out0);
  and and_6 (and_6_out, comparator_6_eq, comparator_7_eq);
  \Contador_de_posicao_da_cabeça_da_cobra  \contador_de_posicao_da_cabeça_da_cobra_1  (
    .Tamanho_da_cobrinha(Tamanho_da_cobrinha), .\Inicialização_com_dados (Inicializador_da_cabeca_da_cobra),
    .\Incremento_de_informações (Incremento_da_cabeca),
    .\Localização_da_cabeça (Posicao_da_cabeca_da_cobrinha));  // open: Looping_de_repetição
  or or_6 (or_6_out, Desenha_maca, Display_clock);
  and and_7 (and_7_out, and_6_out, demultiplexer_5_out1, ~comparator_3_eq);  // AND_Gate
  or or_7 (M4, and_5_out, M4__2);
  Comparator #(.mode("unsigned")) comparator_8 (.a(Tamanho_da_cobrinha), .b(8'h32), .gt(Venceu));  // open: eq, lt
  D_Flip_Flop d_ff_1 (.clk(and_7_out), .D(and_7_out), .Q(Perdeu));  // open: Qn, preset, en, reset
  Contador_do_tamanho_da_cobra contador_do_tamanho_da_cobra_1 (
    .\Inicialização (Inicializador_de_tamanho),
    .Incremento_do_tamanho_da_cobrinha(Incrementa_tamanho_da_cobrinha),
    .\Saída_do_tamanho_da_cobrinha (Tamanho_da_cobrinha));

  // Other names for the same wires on the sheet: reset__x__y = M2

  // Notes on the sheet:
  //   FESA - Faculdade Engenheiro Salvador Arena
  //   Enzo Brito Alves de Oliveira - RA: 082220040
  //   Erikson Vieira Queiroz - RA: 082220021
  //   Heitor Santos Ferreira - RA: 081230042
  //   William Santim - RA: 082220033
  //   Arquitetura de Computadores - N2.B2
  //   CEFSA - Centro Educacional da Fundação Salvador Arena
  //   Engenharia de Computação - Sexto Semestre - EC6
  //   Para iniciar: Pressione CTRL + K
  //   Para reset: Pressione CTRL + R
endmodule

module ORer__8_bits (
  input  [7:0] in_1,
  input  [7:0] in_2,
  output [7:0] out_3
);

  or or_1 (out_3[0], in_1[0], in_2[0]);
  or or_2 (out_3[1], in_1[1], in_2[1]);
  or or_3 (out_3[2], in_1[2], in_2[2]);
  or or_4 (out_3[3], in_1[3], in_2[3]);
  or or_5 (out_3[4], in_1[4], in_2[4]);
  or or_6 (out_3[5], in_1[5], in_2[5]);
  or or_7 (out_3[6], in_1[6], in_2[6]);
  or or_8 (out_3[7], in_1[7], in_2[7]);
endmodule

module ORer__4_bits (
  input  [3:0] in_1,
  input  [3:0] in_2,
  output [3:0] out_3
);

  or or_1 (out_3[0], in_1[0], in_2[0]);
  or or_2 (out_3[1], in_1[1], in_2[1]);
  or or_3 (out_3[2], in_1[2], in_2[2]);
  or or_4 (out_3[3], in_1[3], in_2[3]);
endmodule

module ORed_Register (
  input  [31:0] \Informação_para_escrever ,
  input  Clock,
  input  [4:0] Linha__para_null,
  input  Reseta_a_linha_num,
  output [31:0] out_5
);

  wire not_1_out, or_1_out;
  wire [31:0] ander_32_bits_1_out_3, controlled_buffer_1_out, not_2_out, orer_32_bits_1_out_3, shifter_1_out;

  ORer__32_bits orer_32_bits_1 (.in_1(\Informação_para_escrever ), .in_2(out_5), .out_3(orer_32_bits_1_out_3));
  assign controlled_buffer_1_out = not_1_out ? orer_32_bits_1_out_3 : 32'bz;  // Controlled_Buffer controlled_buffer_1
  not not_1 (not_1_out, Reseta_a_linha_num);
  or or_1 (or_1_out, Reseta_a_linha_num, Clock);
  Register #(.width(32), .trigger("high")) register_1 (
    .D(controlled_buffer_1_out), .Q(out_5), .clk(or_1_out));  // open: en, clr
  Shifter #(.width(32)) shifter_1 (.in(32'h1), .\dist (Linha__para_null), .out(shifter_1_out));
  ANDer__32_bits ander_32_bits_1 (.in_1(out_5), .in_2(not_2_out), .out_3(ander_32_bits_1_out_3));
  assign not_2_out = ~shifter_1_out;  // NOT_Gate not_2, 32 bits wide
  assign controlled_buffer_1_out = Reseta_a_linha_num ? ander_32_bits_1_out_3 : 32'bz;  // Controlled_Buffer controlled_buffer_2
endmodule

module Display_de_exibicao_unitaria (
  input  [4:0] \Posição_em_Y ,
  input  [1:0] \Posição_em_X ,
  input  Clock,
  input  [1:0] Reset_coluna_num,
  input  [4:0] reset_linha_num,
  input  Reset__x__y,
  output [31:0] \Saída_em_tela ,
  output [31:0] \Saída_em_tela_2 ,
  output [31:0] \Saída_em_tela_3 ,
  output [31:0] \Saída_em_tela_4 
);

  wire demultiplexer_2_out0, demultiplexer_2_out1, demultiplexer_2_out2, demultiplexer_2_out3,
       demultiplexer_3_out0, demultiplexer_3_out1, demultiplexer_3_out2, demultiplexer_3_out3;
  wire [31:0] demultiplexer_1_out0, demultiplexer_1_out1, demultiplexer_1_out2, demultiplexer_1_out3,
       shifter_1_out;

  Demultiplexer #(.select(2), .width(32)) demultiplexer_1 (
    .out0(demultiplexer_1_out0), .out1(demultiplexer_1_out1), .out2(demultiplexer_1_out2),
    .out3(demultiplexer_1_out3), .in(shifter_1_out), .sel(\Posição_em_X ));  // open: en
  Shifter #(.width(32)) shifter_1 (.in(32'h1), .\dist (\Posição_em_Y ), .out(shifter_1_out));
  Demultiplexer #(.select(2)) demultiplexer_2 (
    .out0(demultiplexer_2_out0), .out1(demultiplexer_2_out1), .out2(demultiplexer_2_out2),
    .out3(demultiplexer_2_out3), .in(Clock), .sel(\Posição_em_X ));  // open: en
  ORed_Register ored_register_1 (
    .\Informação_para_escrever (demultiplexer_1_out0), .Clock(demultiplexer_2_out0),
    .Linha__para_null(reset_linha_num), .Reseta_a_linha_num(demultiplexer_3_out0), .out_5(\Saída_em_tela ));
  ORed_Register ored_register_2 (
    .\Informação_para_escrever (demultiplexer_1_out1), .Clock(demultiplexer_2_out1),
    .Linha__para_null(reset_linha_num), .Reseta_a_linha_num(demultiplexer_3_out1), .out_5(\Saída_em_tela_2 ));
  ORed_Register ored_register_3 (
    .\Informação_para_escrever (demultiplexer_1_out2), .Clock(demultiplexer_2_out2),
    .Linha__para_null(reset_linha_num), .Reseta_a_linha_num(demultiplexer_3_out2), .out_5(\Saída_em_tela_3 ));
  ORed_Register ored_register_4 (
    .\Informação_para_escrever (demultiplexer_1_out3), .Clock(demultiplexer_2_out3),
    .Linha__para_null(reset_linha_num), .Reseta_a_linha_num(demultiplexer_3_out3), .out_5(\Saída_em_tela_4 ));
  Demultiplexer #(.select(2)) demultiplexer_3 (
    .out0(demultiplexer_3_out0), .out1(demultiplexer_3_out1), .out2(demultiplexer_3_out2),
    .out3(demultiplexer_3_out3), .in(Reset__x__y), .sel(Reset_coluna_num));  // open: en

  // Notes on the sheet:
  //   Memory in
  //   Memory in
endmodule

module Circuito_de_exibicao_em_tela__8_bits (
  input  [4:0] Y_Positions,
  input  [2:0] X_Positions,
  input  Clock,
  input  [2:0] Reset_coluna_num,
  input  [4:0] Reset_linha_num,
  input  Reset__x__y,
  output [31:0] \Saída_em_tela ,
  output [31:0] \Saída_em_tela_2 ,
  output [31:0] \Saída_em_tela_3 ,
  output [31:0] \Saída_em_tela_4 ,
  output [31:0] \Saída_em_tela_5 ,
  output [31:0] \Saída_em_tela_6 ,
  output [31:0] \Saída_em_tela_7 ,
  output [31:0] \Saída_em_tela_8 
);

  wire demultiplexer_1_out0, demultiplexer_1_out1, demultiplexer_2_out0, demultiplexer_2_out1;

  Demultiplexer demultiplexer_1 (
    .out0(demultiplexer_1_out0), .out1(demultiplexer_1_out1), .in(Clock), .sel(X_Positions[2]));  // open: en
  Display_de_exibicao_unitaria display_de_exibicao_unitaria_1 (
    .\Posição_em_Y (Y_Positions), .\Posição_em_X (X_Positions[1:0]), .Clock(demultiplexer_1_out0),
    .Reset_coluna_num(Reset_coluna_num[1:0]), .reset_linha_num(Reset_linha_num),
    .Reset__x__y(demultiplexer_2_out0), .\Saída_em_tela (\Saída_em_tela ),
    .\Saída_em_tela_2 (\Saída_em_tela_2 ), .\Saída_em_tela_3 (\Saída_em_tela_3 ),
    .\Saída_em_tela_4 (\Saída_em_tela_4 ));
  Display_de_exibicao_unitaria display_de_exibicao_unitaria_2 (
    .\Posição_em_Y (Y_Positions), .\Posição_em_X (X_Positions[1:0]), .Clock(demultiplexer_1_out1),
    .Reset_coluna_num(Reset_coluna_num[1:0]), .reset_linha_num(Reset_linha_num),
    .Reset__x__y(demultiplexer_2_out1), .\Saída_em_tela (\Saída_em_tela_5 ),
    .\Saída_em_tela_2 (\Saída_em_tela_6 ), .\Saída_em_tela_3 (\Saída_em_tela_7 ),
    .\Saída_em_tela_4 (\Saída_em_tela_8 ));
  Demultiplexer demultiplexer_2 (
    .out0(demultiplexer_2_out0), .out1(demultiplexer_2_out1), .in(Reset__x__y), .sel(Reset_coluna_num[2]));  // open: en
endmodule

module Alternador_de_memoria (
  input  [3:0] Tamanho_da_cobrinha,
  input  [3:0] \Posição_de_inicio ,
  input  [2:0] \Entrada_de_informação ,
  input  Clock,
  output [3:0] \Endereço_de_saída ,
  output [2:0] \Saída_de_informação ,
  output \Clock_de_saída_para_memória ,
  output \Ponto_de_finalização 
);

  wire and_1_out, comparator_1_eq;
  wire [3:0] counter_1_q;

  Counter #(.width(4), .max('hf), .trigger("falling")) counter_1 (
    .Q(counter_1_q), .clk(Clock), .clr(\Ponto_de_finalização ));  // open: load, D, count, carry
  Adder #(.width(4)) adder_1 (.a(\Posição_de_inicio ), .b(counter_1_q), .out(\Endereço_de_saída ));  // open: cin, cout
  Comparator #(.width(4)) comparator_1 (
    .a(Tamanho_da_cobrinha), .b(\Endereço_de_saída ), .eq(comparator_1_eq));  // open: gt, lt
  Register #(.width(3)) register_1 (
    .D(\Entrada_de_informação ), .Q(\Saída_de_informação ), .clk(Clock));  // open: en, clr
  and and_1 (and_1_out, comparator_1_eq, Clock);
  Counter #(.width(1), .max('h1), .trigger("falling")) counter_2 (
    .Q(\Ponto_de_finalização ), .clk(and_1_out), .clr(\Ponto_de_finalização ));  // open: load, D, count, carry

  assign \Clock_de_saída_para_memória  = Clock;
endmodule

module ORer__3_bits (
  input  [2:0] in_1,
  input  [2:0] in_2,
  output [2:0] out_3
);

  or or_1 (out_3[0], in_1[0], in_2[0]);
  or or_2 (out_3[1], in_1[1], in_2[1]);
  or or_3 (out_3[2], in_1[2], in_2[2]);
endmodule

module OR_gate___3_bits (
  input  [2:0] in_1,
  output out_2
);

  or or_1 (out_2, in_1[0], in_1[1], in_1[2]);
endmodule

module Contador_limitador (
  input  [7:0] Tamanho_da_cobrinha,
  input  Incremento,
  output [7:0] \Localização__Saída ,
  output Looping
);

  Counter #(.trigger("falling")) counter_1 (
    .Q(\Localização__Saída ), .clk(Incremento), .clr(Looping));  // open: load, D, count, carry
  Comparator #(.mode("unsigned")) comparator_1 (
    .a(Tamanho_da_cobrinha), .b(\Localização__Saída ), .eq(Looping));  // open: gt, lt
endmodule

module Contador_do_tamanho_da_cobra (
  input  \Inicialização ,
  input  Incremento_do_tamanho_da_cobrinha,
  output [7:0] \Saída_do_tamanho_da_cobrinha 
);

  wire not_1_out, or_1_out;

  Counter Tamanho_da_cobrinha (
    .load(\Inicialização ), .D(8'h2), .count(not_1_out), .Q(\Saída_do_tamanho_da_cobrinha ), .clk(or_1_out));  // open: carry, clr
  not not_1 (not_1_out, \Inicialização );
  or or_1 (or_1_out, \Inicialização , Incremento_do_tamanho_da_cobrinha);
endmodule

module Modulo_de_exibicao_em_tela (
  input  [7:0] Tamnho_da_cobrinha__entrada,
  input  Clock__entrada,
  output [7:0] \Localização_da_saída ,
  output \Clock__saída ,
  output \Ponto_de_finalização_do_pulso_do_clock 
);

  Contador_limitador contador_limitador_1 (
    .Tamanho_da_cobrinha(Tamnho_da_cobrinha__entrada), .Incremento(Clock__entrada),
    .\Localização__Saída (\Localização_da_saída ));  // open: Looping
  Counter #(.width(1), .max('h1), .trigger("falling")) counter_1 (
    .Q(\Ponto_de_finalização_do_pulso_do_clock ), .clk(Clock__entrada),
    .clr(\Ponto_de_finalização_do_pulso_do_clock ));  // open: load, D, count, carry

  assign \Clock__saída  = Clock__entrada;
endmodule

module \Contador_de_posicao_da_cabeça_da_cobra  (
  input  [7:0] Tamanho_da_cobrinha,
  input  \Inicialização_com_dados ,
  input  \Incremento_de_informações ,
  output [7:0] \Localização_da_cabeça ,
  output \Looping_de_repetição 
);

  wire not_1_out, or_1_out;
  wire [7:0] subtractor_1_out;

  Subtractor subtractor_1 (.a(Tamanho_da_cobrinha), .b(8'h1), .out(subtractor_1_out));  // open: bin, bout
  Counter counter_1 (
    .load(\Inicialização_com_dados ), .D(subtractor_1_out), .count(not_1_out), .Q(\Localização_da_cabeça ),
    .clk(or_1_out), .clr(\Looping_de_repetição ));  // open: carry
  not not_1 (not_1_out, \Inicialização_com_dados );
  or or_1 (or_1_out, \Inicialização_com_dados , \Incremento_de_informações );
  Comparator #(.mode("unsigned")) comparator_1 (
    .a(Tamanho_da_cobrinha), .b(\Localização_da_cabeça ), .eq(\Looping_de_repetição ));  // open: gt, lt
endmodule

module Modulo_de_movimentacao_da_cobra (
  input  Clock__entrada,
  input  [4:0] \Coordenada_da_cabeça_em_Y ,
  input  [4:0] \Coordenada_da_cabeça_em_X ,
  input  [4:0] \Direção_em_X ,
  input  [4:0] \Direção_em_Y ,
  output [4:0] Nova_coordenada_em_Y,
  output [4:0] Nova_coordenada_de_X,
  output \Incremento_da_cabeça_da_cobrinha___Conta_a_posição_da_mesma ,
  output out_9
);

  wire [4:0] \Posição_da_cabeça_em_X_q , \Posição_da_cabeça_em_Y_q ;

  Register #(.width(5)) \Posição_da_cabeça_em_X  (
    .D(\Coordenada_da_cabeça_em_X ), .Q(\Posição_da_cabeça_em_X_q ), .clk(Clock__entrada));  // open: en, clr
  Adder #(.width(5)) adder_1 (
    .a(\Posição_da_cabeça_em_X_q ), .b(\Direção_em_X ), .out(Nova_coordenada_de_X));  // open: cin, cout
  Register #(.width(5)) \Posição_da_cabeça_em_Y  (
    .D(\Coordenada_da_cabeça_em_Y ), .Q(\Posição_da_cabeça_em_Y_q ), .clk(Clock__entrada));  // open: en, clr
  Adder #(.width(5)) adder_2 (
    .a(\Posição_da_cabeça_em_Y_q ), .b(\Direção_em_Y ), .out(Nova_coordenada_em_Y));  // open: cin, cout
  Counter #(.width(1), .max('h1), .trigger("falling")) counter_1 (
    .Q(out_9), .clk(Clock__entrada), .clr(out_9));  // open: load, D, count, carry

  assign \Incremento_da_cabeça_da_cobrinha___Conta_a_posição_da_mesma  = Clock__entrada;
endmodule

module Modulo_de_controle_do_teclado (
  input  [6:0] Teclado,
  input  D,
  input  in_3,
  input  A,
  input  S,
  input  W,
  output Parte_de_Reset,
  output [4:0] \Direção_Eixo_X ,
  output [4:0] \Direção_Eixo_Y 
);

  wire and_1_out, and_2_out, comparator_1_eq, comparator_2_eq, comparator_3_eq, comparator_4_eq,
       comparator_5_eq, comparator_6_eq, Eixo_X_direcional, Eixo_Y_direcional, or_1_out, or_3_out, or_4_out,
       or_5_out, or_6_out, or_9_out, or_10_out;
  wire [4:0] multiplexer_1_out, multiplexer_2_out;

  or or_1 (or_1_out, in_3, D);
  or or_2 (Parte_de_Reset, Eixo_Y_direcional, Eixo_X_direcional);
  Comparator #(.width(7)) comparator_1 (.a(Teclado), .b(7'b1100001), .eq(comparator_1_eq));  // open: gt, lt
  Comparator #(.width(7)) comparator_2 (.a(Teclado), .b(7'b1100100), .eq(comparator_2_eq));  // open: gt, lt
  Comparator #(.width(7)) comparator_3 (.a(Teclado), .b(7'b1110111), .eq(comparator_3_eq));  // open: gt, lt
  Comparator #(.width(7)) comparator_4 (.a(Teclado), .b(7'b1110011), .eq(comparator_4_eq));  // open: gt, lt
  or or_3 (or_3_out, comparator_1_eq, A);
  or or_4 (or_4_out, or_1_out, comparator_2_eq);
  or or_5 (or_5_out, comparator_3_eq, W);
  or or_6 (or_6_out, S, comparator_4_eq);
  or or_7 (Eixo_Y_direcional, or_3_out, or_4_out);
  or or_8 (Eixo_X_direcional, or_6_out, or_5_out);
  Multiplexer #(.width(5)) multiplexer_1 (
    .in0({5{1'b1}}), .in1(5'b00001), .out(multiplexer_1_out), .sel(or_4_out));  // open: en
  or or_9 (or_9_out, or_4_out, or_3_out);
  Comparator #(.width(5), .mode("unsigned")) comparator_5 (
    .a(\Direção_Eixo_X ), .b({5{1'b0}}), .eq(comparator_5_eq));  // open: gt, lt
  Comparator #(.width(5), .mode("unsigned")) comparator_6 (
    .a({5{1'b0}}), .b(\Direção_Eixo_Y ), .eq(comparator_6_eq));  // open: gt, lt
  Multiplexer #(.width(5)) multiplexer_2 (
    .in0(5'b00001), .in1({5{1'b1}}), .out(multiplexer_2_out), .sel(or_6_out));  // open: en
  or or_10 (or_10_out, or_6_out, or_5_out);
  Register #(.width(5), .trigger("falling")) register_1 (
    .D(multiplexer_1_out), .Q(\Direção_Eixo_X ), .clk(and_1_out), .clr(and_2_out));  // open: en
  and and_1 (and_1_out, or_9_out, comparator_5_eq);
  Register #(.width(5), .trigger("falling")) register_2 (
    .D(multiplexer_2_out), .Q(\Direção_Eixo_Y ), .clk(and_2_out), .clr(and_1_out));  // open: en
  and and_2 (and_2_out, comparator_6_eq, or_10_out);
endmodule

module Registrador_de_inicializacao (
  input  [2:0] Valor_iniciado,
  input  Initialize,
  input  [2:0] \Dado__Valor_é_armazenado_no_trigger ,
  input  \Clear_assincrono__Quando_1__o_valor_do_item_é_0_paralelamente ,
  input  \Clock__Valor_é_atualizado_no_trigger ,
  output [2:0] \Saída__Registra_o_valor_atual 
);

  wire or_1_out;
  wire [2:0] controlled_buffer_1_out;

  assign controlled_buffer_1_out = \Clock__Valor_é_atualizado_no_trigger  ? \Dado__Valor_é_armazenado_no_trigger  : 3'bz;  // Controlled_Buffer controlled_buffer_1
  assign controlled_buffer_1_out = Initialize ? Valor_iniciado : 3'bz;  // Controlled_Buffer controlled_buffer_2
  Register #(.width(3)) register_1 (
    .D(controlled_buffer_1_out), .Q(\Saída__Registra_o_valor_atual ), .clk(or_1_out),
    .clr(\Clear_assincrono__Quando_1__o_valor_do_item_é_0_paralelamente ));  // open: en
  or or_1 (or_1_out, Initialize, \Clock__Valor_é_atualizado_no_trigger );
endmodule

module Contador__1_16 (
  input  Clock_de_entrada,
  output \Clock_de_saída 
);

  Counter #(.width(4), .max('hf)) counter_1 (
    .carry(\Clock_de_saída ), .clk(Clock_de_entrada));  // open: load, D, count, Q, clr
endmodule

module ANDer__8_bits (
  input  [7:0] in_1,
  input  [7:0] in_2,
  output [7:0] out_3
);

  and and_1 (out_3[0], in_1[0], in_2[0]);
  and and_2 (out_3[1], in_1[1], in_2[1]);
  and and_3 (out_3[2], in_1[2], in_2[2]);
  and and_4 (out_3[3], in_1[3], in_2[3]);
  and and_5 (out_3[4], in_1[4], in_2[4]);
  and and_6 (out_3[5], in_1[5], in_2[5]);
  and and_7 (out_3[6], in_1[6], in_2[6]);
  and and_8 (out_3[7], in_1[7], in_2[7]);
endmodule

module Modulo_de_crescimento_da_cobra (
  input  [7:0] Tamanho_da_cobrinha,
  input  [7:0] \Posição_de_inicio ,
  input  [4:0] X,
  input  [4:0] Y,
  input  Clock,
  output \Ponto_de_saída_do_clock ,
  output [7:0] \Endereço_de_saída ,
  output [4:0] \Saída_de_X ,
  output [4:0] \Saída_de_Y ,
  output Marco_final
);

  Alternador_de_memoria__32_bits alternador_de_memoria_32_bits_1 (
    .Tamanho_da_cobrinha(Tamanho_da_cobrinha), .Starting_position(\Posição_de_inicio ), .Entrada(X),
    .Clock_de_entrada(Clock), .\Clock_de_saída (\Ponto_de_saída_do_clock ),
    .\Endereço_de_saída (\Endereço_de_saída ), .\Saída (\Saída_de_X ));  // open: Marco_de_parada
  Alternador_de_memoria__32_bits alternador_de_memoria_32_bits_2 (
    .Tamanho_da_cobrinha(Tamanho_da_cobrinha), .Starting_position(\Posição_de_inicio ), .Entrada(Y),
    .Clock_de_entrada(Clock), .Marco_de_parada(Marco_final), .\Saída (\Saída_de_Y ));  // open: Clock_de_saída, Endereço_de_saída
endmodule

module ORer__32_bits (
  input  [31:0] in_1,
  input  [31:0] in_2,
  output [31:0] out_3
);

  ORer__8_bits orer_8_bits_1 (.in_1(in_1[7:0]), .in_2(in_2[7:0]), .out_3(out_3[7:0]));
  ORer__8_bits orer_8_bits_2 (.in_1(in_1[15:8]), .in_2(in_2[15:8]), .out_3(out_3[15:8]));
  ORer__8_bits orer_8_bits_3 (.in_1(in_1[23:16]), .in_2(in_2[23:16]), .out_3(out_3[23:16]));
  ORer__8_bits orer_8_bits_4 (.in_1(in_1[31:24]), .in_2(in_2[31:24]), .out_3(out_3[31:24]));
endmodule

module ANDer__32_bits (
  input  [31:0] in_1,
  input  [31:0] in_2,
  output [31:0] out_3
);

  ANDer__8_bits ander_8_bits_1 (.in_1(in_1[7:0]), .in_2(in_2[7:0]), .out_3(out_3[7:0]));
  ANDer__8_bits ander_8_bits_2 (.in_1(in_1[15:8]), .in_2(in_2[15:8]), .out_3(out_3[15:8]));
  ANDer__8_bits ander_8_bits_3 (.in_1(in_1[23:16]), .in_2(in_2[23:16]), .out_3(out_3[23:16]));
  ANDer__8_bits ander_8_bits_4 (.in_1(in_1[31:24]), .in_2(in_2[31:24]), .out_3(out_3[31:24]));
endmodule

module Alternador_de_memoria__32_bits (
  input  [7:0] Tamanho_da_cobrinha,
  input  [7:0] Starting_position,
  input  [4:0] Entrada,
  input  Clock_de_entrada,
  output [7:0] \Endereço_de_saída ,
  output [4:0] \Saída ,
  output \Clock_de_saída ,
  output Marco_de_parada
);

  wire and_1_out, comparator_1_eq;
  wire [7:0] counter_1_q;

  Counter #(.trigger("falling")) counter_1 (
    .Q(counter_1_q), .clk(Clock_de_entrada), .clr(Marco_de_parada));  // open: load, D, count, carry
  Adder adder_1 (.a(Starting_position), .b(counter_1_q), .out(\Endereço_de_saída ));  // open: cin, cout
  Comparator #(.mode("unsigned")) comparator_1 (
    .a(Tamanho_da_cobrinha), .b(\Endereço_de_saída ), .eq(comparator_1_eq));  // open: gt, lt
  Register #(.width(5)) register_1 (.D(Entrada), .Q(\Saída ), .clk(Clock_de_entrada));  // open: en, clr
  and and_1 (and_1_out, comparator_1_eq, Clock_de_entrada);
  Counter #(.width(1), .max('h1), .trigger("falling")) counter_2 (
    .Q(Marco_de_parada), .clk(and_1_out), .clr(Marco_de_parada));  // open: load, D, count, carry

  assign \Clock_de_saída  = Clock_de_entrada;
endmodule

module Circuito_de_exibicao_em_tela__32_bits (
  input  Clock,
  input  [4:0] \Posições_em_Y ,
  input  [4:0] \Posições_em_X ,
  input  [4:0] Reseta_a_coluna_numerada_em_uso,
  input  [4:0] Reseta_a_linha_numerada_em_uso,
  input  Reseta_os_eixos__x__e__y,
  output [31:0] out_7,
  output [31:0] out_8,
  output [31:0] out_9,
  output [31:0] out_10,
  output [31:0] out_11,
  output [31:0] out_12,
  output [31:0] out_13,
  output [31:0] out_14,
  output [31:0] out_15,
  output [31:0] out_16,
  output [31:0] out_17,
  output [31:0] out_18,
  output [31:0] out_19,
  output [31:0] out_20,
  output [31:0] out_21,
  output [31:0] out_22,
  output [31:0] out_23,
  output [31:0] out_24,
  output [31:0] out_25,
  output [31:0] out_26,
  output [31:0] out_27,
  output [31:0] out_28,
  output [31:0] out_29,
  output [31:0] out_30,
  output [31:0] out_31,
  output [31:0] out_32,
  output [31:0] out_33,
  output [31:0] out_34,
  output [31:0] out_35,
  output [31:0] out_36,
  output [31:0] out_37,
  output [31:0] out_38
);

  wire demultiplexer_1_out0, demultiplexer_1_out1, demultiplexer_1_out2, demultiplexer_1_out3,
       demultiplexer_2_out0, demultiplexer_2_out1, demultiplexer_2_out2, demultiplexer_2_out3;

  Demultiplexer #(.select(2)) demultiplexer_1 (
    .out0(demultiplexer_1_out0), .out1(demultiplexer_1_out1), .out2(demultiplexer_1_out2),
    .out3(demultiplexer_1_out3), .in(Clock), .sel(\Posições_em_X [4:3]));  // open: en
  Circuito_de_exibicao_em_tela__8_bits circuito_de_exibicao_em_tela_8_bits_1 (
    .Y_Positions(\Posições_em_Y ), .X_Positions(\Posições_em_X [2:0]), .Clock(demultiplexer_1_out0),
    .Reset_coluna_num(Reseta_a_coluna_numerada_em_uso[2:0]),
    .Reset_linha_num(Reseta_a_linha_numerada_em_uso), .Reset__x__y(demultiplexer_2_out0),
    .\Saída_em_tela (out_7), .\Saída_em_tela_2 (out_8), .\Saída_em_tela_3 (out_9),
    .\Saída_em_tela_4 (out_10), .\Saída_em_tela_5 (out_11), .\Saída_em_tela_6 (out_12),
    .\Saída_em_tela_7 (out_13), .\Saída_em_tela_8 (out_14));
  Circuito_de_exibicao_em_tela__8_bits circuito_de_exibicao_em_tela_8_bits_2 (
    .Y_Positions(\Posições_em_Y ), .X_Positions(\Posições_em_X [2:0]), .Clock(demultiplexer_1_out1),
    .Reset_coluna_num(Reseta_a_coluna_numerada_em_uso[2:0]),
    .Reset_linha_num(Reseta_a_linha_numerada_em_uso), .Reset__x__y(demultiplexer_2_out1),
    .\Saída_em_tela (out_15), .\Saída_em_tela_2 (out_16), .\Saída_em_tela_3 (out_17),
    .\Saída_em_tela_4 (out_18), .\Saída_em_tela_5 (out_19), .\Saída_em_tela_6 (out_20),
    .\Saída_em_tela_7 (out_21), .\Saída_em_tela_8 (out_22));
  Circuito_de_exibicao_em_tela__8_bits circuito_de_exibicao_em_tela_8_bits_3 (
    .Y_Positions(\Posições_em_Y ), .X_Positions(\Posições_em_X [2:0]), .Clock(demultiplexer_1_out2),
    .Reset_coluna_num(Reseta_a_coluna_numerada_em_uso[2:0]),
    .Reset_linha_num(Reseta_a_linha_numerada_em_uso), .Reset__x__y(demultiplexer_2_out2),
    .\Saída_em_tela (out_23), .\Saída_em_tela_2 (out_24), .\Saída_em_tela_3 (out_25),
    .\Saída_em_tela_4 (out_26), .\Saída_em_tela_5 (out_27), .\Saída_em_tela_6 (out_28),
    .\Saída_em_tela_7 (out_29), .\Saída_em_tela_8 (out_30));
  Circuito_de_exibicao_em_tela__8_bits circuito_de_exibicao_em_tela_8_bits_4 (
    .Y_Positions(\Posições_em_Y ), .X_Positions(\Posições_em_X [2:0]), .Clock(demultiplexer_1_out3),
    .Reset_coluna_num(Reseta_a_coluna_numerada_em_uso[2:0]),
    .Reset_linha_num(Reseta_a_linha_numerada_em_uso), .Reset__x__y(demultiplexer_2_out3),
    .\Saída_em_tela (out_31), .\Saída_em_tela_2 (out_32), .\Saída_em_tela_3 (out_33),
    .\Saída_em_tela_4 (out_34), .\Saída_em_tela_5 (out_35), .\Saída_em_tela_6 (out_36),
    .\Saída_em_tela_7 (out_37), .\Saída_em_tela_8 (out_38));
  Demultiplexer #(.select(2)) demultiplexer_2 (
    .out0(demultiplexer_2_out0), .out1(demultiplexer_2_out1), .out2(demultiplexer_2_out2),
    .out3(demultiplexer_2_out3), .in(Reseta_os_eixos__x__e__y), .sel(Reseta_a_coluna_numerada_em_uso[4:3]));  // open: en
endmodule

module Exibicao_do_digito_da_coordenada_da_maca (
  input  [4:0] in_1,
  input  [4:0] in_2,
  output [3:0] out_3,
  output [3:0] out_4,
  output [3:0] out_5,
  output [3:0] out_6
);


  assign out_3 = {3'b000, in_1[4]};
  assign out_4 = in_1[3:0];
  assign out_5 = {3'b000, in_2[4]};
  assign out_6 = in_2[3:0];
endmodule
